# Fritzing sketch PCB_PCF8574_02 (saved by Fritzing 0.9.3b)
circuit board: 3.31283cm x 4.44148cm
breadboards: 1

parts:
  U1 = PCF8574 [package="DIP16 [THT]"]
  Componente1 = Arduino Uno (Rev3)
  INT_SDA_SCL = female pin header, 3 pins [form="♀ (female)"]
  P4-P7 = female pin header, 4 pins [form="♀ (female)"]
  P0-P3 = female pin header, 4 pins [form="♀ (female)"]
  R1 = Resistor [tolerance=±5% resistance=10k package=THT]
  R2 = Resistor [tolerance=±5% resistance=10k package=THT]
  R3 = Resistor [tolerance=±5% resistance=10k package=THT]
  SW1 = DIP SWITCH [package=dipswitch-02]
  SW2 = DIP SWITCH [package=dipswitch-02]
  R4 = Resistor [tolerance=±5% resistance=10k package=THT]
  R5 = Resistor [tolerance=±5% resistance=10k package=THT]
  R6 = Resistor [tolerance=±5% resistance=10k package=THT]
  Power_from_controller = female pin header, 2 pins [form="♀ (female)"]

nets:
  N1: U1.A0, SW1.1, R4.Pin_0
  N2: U1.A1, SW1.2, SW2.1, R5.Pin_0
  N3: U1.A3, SW2.2, R6.Pin_0
  N4: U1.P0, P0-P3.pin4
  N5: U1.P1, P0-P3.pin3
  N6: U1.P2, P0-P3.pin2
  N7: U1.P3, P0-P3.pin1
  GND: U1.GND, Componente1.GND, R4.Pin_1, R5.Pin_1, R6.Pin_1, Power_from_controller.pin1
  N8: U1.P4, P4-P7.pin1
  N9: U1.P5, P4-P7.pin2
  N10: U1.P6, P4-P7.pin3
  N11: U1.P7, P4-P7.pin4
  N12: U1.INT, Componente1.D2, INT_SDA_SCL.pin1, R3.Pin_0
  N13: U1.SCL, Componente1.A5/SCL, INT_SDA_SCL.pin2, R2.Pin_0
  N14: U1.SDA, Componente1.A4/SDA, INT_SDA_SCL.pin3, R1.Pin_0
  5V: U1.VCC, Componente1.5V, R1.Pin_1, R2.Pin_1, R3.Pin_1, SW1.3, SW1.4, SW2.3, SW2.4, Power_from_controller.pin2

notes:
  VG
  PCF8574
  Reef
