# Fritzing sketch PCB_PCF8574_02_ic (saved by Fritzing 0.9.3b)
circuit board: 3.31283cm x 4.44148cm
breadboards: 1

parts:
  Componente1 = Arduino Uno (Rev3)
  INT_SDA_SCL = female pin header, 3 pins [form="♀ (female)"]
  P4-P7 = female pin header, 4 pins [form="♀ (female)"]
  P0-P3 = female pin header, 4 pins [form="♀ (female)"]
  R1 = Resistor [tolerance=±5% resistance=10k package=THT]
  R2 = Resistor [tolerance=±5% resistance=10k package=THT]
  R3 = Resistor [tolerance=±5% resistance=10k package=THT]
  SW1 = DIP SWITCH [package=dipswitch-02]
  SW2 = DIP SWITCH [package=dipswitch-02]
  R4 = Resistor [tolerance=±5% resistance=10k package=THT]
  R5 = Resistor [tolerance=±5% resistance=10k package=THT]
  R6 = Resistor [tolerance=±5% resistance=10k package=THT]
  Power_from_controller = female pin header, 2 pins [form="♀ (female)"]
  IC1 = IC, DIP package, 16 pins [chip_label=IC]

nets:
  N1: Componente1.A4/SDA, INT_SDA_SCL.pin3, R1.Pin_0, IC1.pin7
  N2: Componente1.A5/SCL, INT_SDA_SCL.pin2, R2.Pin_0, IC1.pin6
  N3: Componente1.GND, R4.Pin_1, R5.Pin_1, R6.Pin_1, Power_from_controller.pin1, IC1.pin16
  N4: Componente1.D2, INT_SDA_SCL.pin1, R3.Pin_0, IC1.pin5
  N5: Componente1.5V, R1.Pin_1, R2.Pin_1, R3.Pin_1, SW1.3, SW1.4, SW2.3, SW2.4, Power_from_controller.pin2, IC1.pin8
  N6: P4-P7.pin1, IC1.pin1
  N7: P4-P7.pin2, IC1.pin2
  N8: P4-P7.pin3, IC1.pin3
  N9: P4-P7.pin4, IC1.pin4
  N10: P0-P3.pin1, IC1.pin15
  N11: P0-P3.pin2, IC1.pin14
  N12: P0-P3.pin3, IC1.pin13
  N13: P0-P3.pin4, IC1.pin12
  N14: SW1.1, R4.Pin_0, IC1.pin9
  N15: SW1.2, SW2.1, R5.Pin_0, IC1.pin10
  N16: SW2.2, R6.Pin_0, IC1.pin11

notes:
  VG
  PCF8574
  Reef
