# Fritzing sketch PCB_PCF8574_03 (saved by Fritzing 0.9.3b)
circuit board: 3.31283cm x 4.44148cm
breadboards: 1

parts:
  PCF8574 = PCF8574 [package="DIP16 [THT]"]
  Componente1 = Arduino Uno (Rev3)
  INT_SDA_SCL = female pin header, 3 pins [form="♀ (female)"]
  P4-P7 = female pin header, 4 pins [form="♀ (female)"]
  P0-P3 = female pin header, 4 pins [form="♀ (female)"]
  Pull-upp_SCL = Resistor [tolerance=±5% resistance=10k package=THT]
  Pull-up_SDA = Resistor [tolerance=±5% resistance=10k package=THT]
  Pull-up_int = Resistor [tolerance=±5% resistance=10k package=THT]
  Adress_i2c = DIP SWITCH [package=dipswitch-02]
  SW2 = DIP SWITCH [package=dipswitch-02]
  Pull-down_res_A0 = Resistor [tolerance=±5% resistance=10k package=THT]
  Pull-down_res_A1 = Resistor [tolerance=±5% resistance=10k package=THT]
  Pull-down_res_A2 = Resistor [tolerance=±5% resistance=10k package=THT]
  Power_from_controller = female pin header, 2 pins [form="♀ (female)"]

nets:
  N1: PCF8574.A0, Adress_i2c.1, Pull-down_res_A0.Pin_0
  N2: PCF8574.A1, Adress_i2c.2, SW2.1, Pull-down_res_A1.Pin_0
  N3: PCF8574.A3, SW2.2, Pull-down_res_A2.Pin_0
  N4: PCF8574.P0, P0-P3.pin4
  N5: PCF8574.P1, P0-P3.pin3
  N6: PCF8574.P2, P0-P3.pin2
  N7: PCF8574.P3, P0-P3.pin1
  GND: PCF8574.GND, Componente1.GND, Pull-down_res_A0.Pin_1, Pull-down_res_A1.Pin_1, Pull-down_res_A2.Pin_1, Power_from_controller.pin1
  N8: PCF8574.P4, P4-P7.pin1
  N9: PCF8574.P5, P4-P7.pin2
  N10: PCF8574.P6, P4-P7.pin3
  N11: PCF8574.P7, P4-P7.pin4
  N12: PCF8574.INT, Componente1.D2, INT_SDA_SCL.pin1, Pull-up_int.Pin_0
  N13: PCF8574.SCL, Componente1.A5/SCL, INT_SDA_SCL.pin2, Pull-up_SDA.Pin_0
  N14: PCF8574.SDA, Componente1.A4/SDA, INT_SDA_SCL.pin3, Pull-upp_SCL.Pin_0
  VCC: PCF8574.VCC, Componente1.5V, Pull-upp_SCL.Pin_1, Pull-up_SDA.Pin_1, Pull-up_int.Pin_1, Adress_i2c.3, Adress_i2c.4, SW2.3, SW2.4, Power_from_controller.pin2

notes:
  VG
  PCF8574
  Reef
