# Fritzing sketch PCB_PCF8574_IC (saved by Fritzing 0.9.3b)
circuit board: 2.74415cm x 3.16866cm
breadboards: 1

parts:
  S1 = Toggle Switch [package=THT]
  S2 = Toggle Switch [package=THT]
  S3 = Toggle Switch [package=THT]
  IC1 = IC, DIP package, 16 pins [chip_label=IC]

nets:
  5V: S1.L1, S2.L1, S3.L1, IC1.pin8
  N1: S1.COM, IC1.pin11
  GND: S1.L2, S2.L2, S3.L2, IC1.pin16
  N2: S2.COM, IC1.pin10
  N3: S3.COM, IC1.pin9

notes:
  VG
  PCF8574
