# Fritzing sketch pcf8574SimpleConnection (saved by Fritzing 0.9.3b)
breadboards: 1

parts:
  Part1 = Arduino Uno (Rev3)
  U1 = PCF8574 [package="DIP16 [THT]"]
  R1 = Resistor [tolerance=±5% resistance=10k package=THT]
  R2 = Resistor [tolerance=±5% resistance=10k package=THT]

nets:
  N1: Part1.A4/SDA, U1.SDA, R2.Pin_1
  N2: Part1.A5/SCL, U1.SCL, R1.Pin_1
  N3: Part1.D2, U1.INT
  5V: Part1.5V, U1.VCC, R1.Pin_0, R2.Pin_0
  GND: Part1.GND, U1.A0, U1.A1, U1.A2, U1.GND

notes:
  Address
  Interrupt
  SDA SCL
