# Fritzing sketch testLedArduino (saved by Fritzing 0.9.3b)
breadboards: 1

parts:
  Componente1 = Arduino Uno (Rev3)
  LED3 = LED - 5mm [color="Red (633nm)" current=0.030 package="5 mm [THT]"]
  R8 = Resistor [tolerance=±5% resistance=220 power=0.25 package=THT]
  R9 = Resistor [tolerance=±5% resistance=10k power=0.25 package=THT]
  R10 = Resistor [tolerance=±5% resistance=10k power=0.25 package=THT]
  U1 = PCF8574 [package="DIP16 [THT]"]
  LED4 = LED - 5mm [color="Red (633nm)" current=0.030 package="5 mm [THT]"]
  R12 = Resistor [tolerance=±5% resistance=220 power=0.25 package=THT]
  LED5 = LED - 5mm [color="Red (633nm)" current=0.030 package="5 mm [THT]"]
  R13 = Resistor [tolerance=±5% resistance=220 power=0.25 package=THT]
  LED6 = LED - 5mm [color="Red (633nm)" current=0.030 package="5 mm [THT]"]
  R14 = Resistor [tolerance=±5% resistance=220 power=0.25 package=THT]
  LED7 = LED - 5mm [color="Red (633nm)" current=0.030 package="5 mm [THT]"]
  R15 = Resistor [tolerance=±5% resistance=220 power=0.25 package=THT]
  LED8 = LED - 5mm [color="Red (633nm)" current=0.030 package="5 mm [THT]"]
  R16 = Resistor [tolerance=±5% resistance=220 power=0.25 package=THT]
  LED9 = LED - 5mm [color="Red (633nm)" current=0.030 package="5 mm [THT]"]
  R17 = Resistor [tolerance=±5% resistance=220 power=0.25 package=THT]
  LED10 = LED - 5mm [color="Red (633nm)" current=0.030 package="5 mm [THT]"]
  R18 = Resistor [tolerance=±5% resistance=220 power=0.25 package=THT]

nets:
  N1: Componente1.A4/SDA, R10.Pin_1, U1.SDA
  N2: Componente1.A5/SCL, R9.Pin_1, U1.SCL
  5V: Componente1.5V, R8.Pin_1, R9.Pin_0, R10.Pin_0, U1.VCC, R12.Pin_1, R13.Pin_1, R14.Pin_1, R15.Pin_1, R16.Pin_1, R17.Pin_1, R18.Pin_1
  GND: Componente1.GND, U1.A0, U1.A1, U1.A2, U1.GND
  N3: LED3.cathode, U1.P0
  N4: LED3.anode, R8.Pin_0
  N5: U1.P1, LED4.cathode
  N6: U1.P2, LED5.cathode
  N7: U1.P3, LED6.cathode
  N8: U1.P4, LED7.cathode
  N9: U1.P5, LED8.cathode
  N10: U1.P6, LED9.cathode
  N11: U1.P7, LED10.cathode
  N12: LED4.anode, R12.Pin_0
  N13: LED5.anode, R13.Pin_0
  N14: LED6.anode, R14.Pin_0
  N15: LED7.anode, R15.Pin_0
  N16: LED8.anode, R16.Pin_0
  N17: LED9.anode, R17.Pin_0
  N18: LED10.anode, R18.Pin_0
