# Fritzing sketch testLedESP32 (saved by Fritzing 0.9.3b)
breadboards: 1

parts:
  R8 = Resistor [tolerance=±5% resistance=220 power=0.25 package=THT]
  R9 = Resistor [tolerance=±5% resistance=10k power=0.25 package=THT]
  R10 = Resistor [tolerance=±5% resistance=10k power=0.25 package=THT]
  U1 = PCF8574 [package="DIP16 [THT]"]
  R12 = Resistor [tolerance=±5% resistance=220 power=0.25 package=THT]
  R13 = Resistor [tolerance=±5% resistance=220 power=0.25 package=THT]
  R14 = Resistor [tolerance=±5% resistance=220 power=0.25 package=THT]
  R15 = Resistor [tolerance=±5% resistance=220 power=0.25 package=THT]
  R16 = Resistor [tolerance=±5% resistance=220 power=0.25 package=THT]
  R17 = Resistor [tolerance=±5% resistance=220 power=0.25 package=THT]
  R18 = Resistor [tolerance=±5% resistance=220 power=0.25 package=THT]
  U2 = ESP32S-HiLetgo [part_number=ESP32S-HiLetgo]
  LED10 = LED - 5mm [color="Red (633nm)" current=0.030 package="5 mm [THT]"]
  LED9 = LED - 5mm [color="Red (633nm)" current=0.030 package="5 mm [THT]"]
  LED8 = LED - 5mm [color="Red (633nm)" current=0.030 package="5 mm [THT]"]
  LED7 = LED - 5mm [color="Red (633nm)" current=0.030 package="5 mm [THT]"]
  LED6 = LED - 5mm [color="Red (633nm)" current=0.030 package="5 mm [THT]"]
  LED5 = LED - 5mm [color="Red (633nm)" current=0.030 package="5 mm [THT]"]
  LED4 = LED - 5mm [color="Red (633nm)" current=0.030 package="5 mm [THT]"]
  LED3 = LED - 5mm [color="Red (633nm)" current=0.030 package="5 mm [THT]"]

nets:
  N1: R8.Pin_0, LED3.anode
  N2: R8.Pin_1, R9.Pin_0, R10.Pin_0, U1.VCC, R12.Pin_1, R13.Pin_1, R14.Pin_1, R15.Pin_1, R16.Pin_1, R17.Pin_1, R18.Pin_1, U2.3.3
  N3: R9.Pin_1, U1.SCL, U2.GPIO21
  N4: R10.Pin_1, U1.SDA, U2.GPIO22
  GND: U1.A0, U1.A1, U1.A2, U1.GND, U2.GND
  N5: U1.P0, LED3.cathode
  N6: U1.P1, LED4.cathode
  N7: U1.P2, LED5.cathode
  N8: U1.P3, LED6.cathode
  N9: U1.P4, LED7.cathode
  N10: U1.P5, LED8.cathode
  N11: U1.P6, LED9.cathode
  N12: U1.P7, LED10.cathode
  N13: R12.Pin_0, LED4.anode
  N14: R13.Pin_0, LED5.anode
  N15: R14.Pin_0, LED6.anode
  N16: R15.Pin_0, LED7.anode
  N17: R16.Pin_0, LED8.anode
  N18: R17.Pin_0, LED9.anode
  N19: R18.Pin_0, LED10.anode

custom parts:
  ESP32S-HiLetgo: HiLetgo ESP-WROOM-32 ESP32 ESP-32S Development Board 2.4GHz Dual-Mode WiFi + Bluetooth Dual Cores Microcontroller The ESP32 integrated with Antenna switches, RF Balun, power amplifiers, low-noise amplifiers, filters, and management modules, and the entire solution occupies the least area of PCB. 2.4 GHz Wi-Fi plus Bluetooth dual-mode chip, with TSMC Ultra-low power consumption 40nm technology,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
