# Fritzing sketch testReadWriteLedButton (saved by Fritzing 0.9.3b)
breadboards: 1

parts:
  Componente1 = Arduino Uno (Rev3)
  S2 = Pushbutton [package="[THT]"]
  R2 = Resistor [tolerance=±5% resistance=10k power=0.25 package=THT]
  LED3 = LED - 5mm [color="Red (633nm)" current=0.030 package="5 mm [THT]"]
  R8 = Resistor [tolerance=±5% resistance=220 power=0.25 package=THT]
  R9 = Resistor [tolerance=±5% resistance=10k power=0.25 package=THT]
  R10 = Resistor [tolerance=±5% resistance=10k power=0.25 package=THT]
  R11 = Resistor [tolerance=±5% resistance=10k power=0.25 package=THT]
  U1 = PCF8574 [package="DIP16 [THT]"]

nets:
  N1: Componente1.A4/SDA, R10.Pin_1, U1.SDA
  N2: Componente1.A5/SCL, R9.Pin_1, U1.SCL
  N3: Componente1.D2, R11.Pin_1, U1.INT
  5V: Componente1.5V, S2.Pin_1, S2.Pin_2, R8.Pin_1, R9.Pin_0, R10.Pin_0, R11.Pin_0, U1.A0, U1.VCC
  GND: Componente1.GND, R2.Pin_1, U1.A1, U1.A2, U1.GND
  N4: S2.Pin_3, S2.Pin_4, R2.Pin_0, U1.P0
  N5: LED3.cathode, U1.P1
  N6: LED3.anode, R8.Pin_0
